# Fritzing sketch ultrasonic-theremin (saved by Fritzing 0.9.2b)
breadboards: 1

parts:
  Part1 = Arduino Uno (Rev3)
  Part2 = SRF05 Ultrasonic Rangefinder
  LED1 = smd LED [color="Red (633nm)" package="0603 [SMD]"]
  R1 = Resistor [tolerance=±5% resistance=220 package="0402 [SMD]"]
  LED2 = smd LED [color="Red (633nm)" package="0603 [SMD]"]
  LED3 = smd LED [color="Red (633nm)" package="0603 [SMD]"]
  LED4 = smd LED [color="Yellow (595nm)" package="0603 [SMD]"]
  LED5 = smd LED [color="Yellow (595nm)" package="0603 [SMD]"]
  LED6 = smd LED [color="Green (570nm)" package="0603 [SMD]"]
  LED7 = smd LED [color="Green (570nm)" package="0603 [SMD]"]
  LED8 = smd LED [color="Green (565nm)" package="0603 [SMD]"]
  R2 = Resistor [tolerance=±5% resistance=220 package="0402 [SMD]"]
  R3 = Resistor [tolerance=±5% resistance=220 package="0402 [SMD]"]
  R4 = Resistor [tolerance=±5% resistance=220 package="0402 [SMD]"]
  R5 = Resistor [tolerance=±5% resistance=220 package="0402 [SMD]"]
  R6 = Resistor [tolerance=±5% resistance=220 package="0402 [SMD]"]
  R7 = Resistor [tolerance=±5% resistance=220 package="0402 [SMD]"]
  R8 = Resistor [tolerance=±5% resistance=220 package="0402 [SMD]"]
  J1 = Piezo Speaker

nets:
  N1: Part1.D8, R7.Pin_1
  N2: Part1.D9_PWM, R6.Pin_1
  N3: Part1.D10_PWM/SS, R5.Pin_1
  N4: Part1.D11_PWM/MOSI, R4.Pin_1
  N5: Part1.D12/MISO, R3.Pin_1
  N6: Part1.D13/SCK, R2.Pin_1
  N7: Part1.D3_PWM, J1.pin2
  N8: Part1.D4, Part2.Trig
  N9: Part1.D5_PWM, Part2.Echo
  N10: Part1.D6_PWM, R1.Pin_1
  N11: Part1.D7, R8.Pin_1
  5V: Part1.5V, Part2.VCC
  GND: Part1.GND, Part2.GND, LED1.cathode, LED2.cathode, LED3.cathode, LED4.cathode, LED5.cathode, LED6.cathode, LED7.cathode, LED8.cathode, J1.pin1
  N12: LED1.anode, R2.Pin_0
  N13: R1.Pin_0, LED8.anode
  N14: LED2.anode, R3.Pin_0
  N15: LED3.anode, R4.Pin_0
  N16: LED4.anode, R5.Pin_0
  N17: LED5.anode, R6.Pin_0
  N18: LED6.anode, R7.Pin_0
  N19: LED7.anode, R8.Pin_0
